# Fritzing sketch RLRES (saved by Fritzing 0.9.3b)
circuit board: 5.89309cm x 5.5557cm

parts:
  M1 = RioRand LM2596
  A1 = BBAA100043
  LED1 = 2-digit 7-segment [package=THT-longpads]
  U1 = 74HC595 [package="DIP16 [THT]"]
  Part1 = Arduino Nano (Rev3.0)
  Mod1 = ESP32 - CAM
  Q1 = NPN-Transistor [package="TO92 [THT]"]
  VCC1 = Battery block 9V
  TP1 = TP4056 [chip_label=TP4056 package="DIP (Dual Inline) [THT]"]

nets:
  N1: M1.Pin_1, TP1.pin3
  N2: M1.Pin_2, TP1.pin6
  5V: M1.Pin_3, U1.MR, U1.VCC, Part1.5V, Mod1.5V
  GND: M1.Pin_4, A1.pin4, U1.GND, U1.OE, Part1.GND, Mod1.GND
  N3: A1.pin1, Part1.D13/SCK
  N4: A1.pin2, Part1.D12/MISO
  N5: A1.pin3, Part1.D10, Q1.B
  N6: LED1.A, U1.Q0
  N7: LED1.C, U1.Q2
  N8: LED1.E, U1.Q4
  N9: LED1.D, U1.Q3
  N10: LED1.G, U1.Q6
  N11: LED1.F, U1.Q5
  N12: LED1.DIG2, Part1.D4
  N13: LED1.DIG1, Part1.D5
  N14: LED1.B, U1.Q1
  N15: U1.SH_CP, Part1.D9
  N16: U1.ST_CP, Part1.D8
  N17: U1.DS, Part1.D6
  N18: Mod1.IO13, Q1.C
  N19: Mod1.3V3, Q1.E
  N20: VCC1.-, TP1.pin5
  N21: VCC1.+, TP1.pin4

custom parts:
  BBAA100043: BBAA100043 traffic light module.
  2-digit 7-segment: Most common two-digit seven-segment led indicator you can find on the internet. 10 legs: 2 common electrodes (one per each digit), 8 electrodes of each segment.
  ESP32 - CAM: The ESP32-CAM has a very competitive small-size camera module that can operate independently as a minimum system with a footprint of only 27*40.5*4.5mm and a deep sleep current of up to 6mA.
  TP4056: A DIP stand-in part for whatever IC you want. With 6 pins on a 300mil dual inline package (DIP) footprint.
